// Logisim project RAMLogic.circ as structural Verilog: 1 circuit, main circuit main
module main (
  output out_1
);

  wire [1:0] undriven;
  wire [3:0] ram_1_data, undriven_2, undriven_3, undriven_4, undriven_5;

  RAM #(.addrWidth(10), .dataWidth(4), .databus("bidir"), .trigger("high")) ram_1 (
    .addr({{8{1'b0}}, undriven}), .data(ram_1_data));  // open: we, oe
  Demultiplexer #(.select(2), .width(4)) demultiplexer_1 ();  // open: out0, out1, out2, out3, in, sel
  Controlled_Buffer controlled_buffer_1 (.out(ram_1_data[0]));  // open: in, en
  Controlled_Buffer controlled_buffer_2 (.out(ram_1_data[1]));  // open: in, en
  Demultiplexer #(.select(2)) demultiplexer_2 (.out3(out_1), .in(ram_1_data[1]));  // open: out0, out1, out2, sel
  Controlled_Buffer controlled_buffer_3 (.out(ram_1_data[2]));  // open: in, en
  Controlled_Buffer controlled_buffer_4 (.out(ram_1_data[3]));  // open: in, en
  Demultiplexer #(.select(2)) demultiplexer_3 ();  // open: out0, out1, out2, out3, in, sel
  DotMatrix #(.matrixcols(4), .matrixrows(4)) dotmatrix_1 (
    .col0(undriven_2), .col1(undriven_3), .col2(undriven_4), .col3(undriven_5));
  Demultiplexer #(.select(2), .width(4)) demultiplexer_4 ();  // open: out0, out1, out2, out3, in, sel
endmodule
